# Fritzing sketch Schematic (saved by Fritzing 0.9.3b)
breadboards: 1

parts:
  Raspberry_Pi_1 = Raspberry Pi 3 [part_number=RPI-3-V1.2]
  M1 = MakerFocus MAX30102
  DS2 = DS18B20 1-Wire Temperature Sensor [part_number=DS18B20]
  R1 = Resistor [tolerance=±5% resistance=4.7k package="0402 [SMD]"]

nets:
  3V3: Raspberry_Pi_1.3v3, Raspberry_Pi_1.3V3, M1.VIN, DS2.VDD, R1.Pin_0
  N1: Raspberry_Pi_1.GPIO2, M1.SDA
  N2: Raspberry_Pi_1.GPIO3, M1.SCL
  N3: Raspberry_Pi_1.GPIO4, M1.IRQ, M1.INT
  N4: Raspberry_Pi_1.GPIO17, DS2.DQ, R1.Pin_1
  GND: Raspberry_Pi_1.GND, M1.GND, DS2.GND

custom parts:
  MakerFocus MAX30102: Oximeter module using the MAX30102 chip. As usual, if you want the mounting holes in pcb, you need to drag a hole over the pad in silkscreen to actually drill the hole (by default they are not drilled)
